# Fritzing sketch Nano-to-Batt-Kit (saved by Fritzing 1.0.7)
breadboards: 1

parts:
  Part1 = Arduino Nano (Rev3.0)
  MIST1 = Mist Maker Battery Kit V0.4.1 [part_number=byproductlab-mistmaker-battkit-v041]
  DISC1 = Mist Maker Piezo Disc [part_number="piezo mesh atomizer disc"]  # not connected

nets:
  GND: Part1.GND, MIST1.GND
  N1: Part1.D7, MIST1.D3_/_BOOST_EN
  N2: Part1.D9, MIST1.D0_/_MIST
  N3: Part1.5V, MIST1.5V_in

custom parts:
  Mist Maker Battery Kit V0.4.1: Programmable Mist Maker Battery Kit (OSHWA US002742). Jumper into the empty XIAO socket: minimal mist = GND + D0 (108.7 kHz PWM) + D3 (boost enable HIGH). Use with the MistMaker Arduino library v2.5.0+.
  Mist Maker Piezo Disc: Ultrasonic mesh atomizer disc (108.7 kHz) with molded cable and PH-2.0 plug. Seat the plug into the Mist Maker kits' DISC connector.
