# Fritzing sketch Nano-to-Extension-Kit (saved by Fritzing 1.0.7)
breadboards: 1

parts:
  MIST1 = Mist Maker Extension Kit V0.1 [part_number=byproductlab-mistmaker-extkit-v01]
  DISC1 = Mist Maker Piezo Disc [part_number="piezo mesh atomizer disc"]  # not connected
  Part1 = Arduino Nano (Rev3.0)

nets:
  N1: MIST1.D0_/_MIST, Part1.D9
  N2: MIST1.D3_(n.c.), Part1.D7
  GND: MIST1.GND, Part1.GND
  N3: MIST1.5V_in, Part1.5V

custom parts:
  Mist Maker Extension Kit V0.1: Programmable Mist Maker Extension Kit (OSHWA US002742). Solder 2.54 mm headers into the XIAO footprint, then: 5V + GND + D0 (108.7 kHz PWM) makes mist — no enable pin. Use with the MistMaker Arduino library v2.5.0+.
  Mist Maker Piezo Disc: Ultrasonic mesh atomizer disc (108.7 kHz) with molded cable and PH-2.0 plug. Seat the plug into the Mist Maker kits' DISC connector.
