# Fritzing sketch Uno-to-Batt-Kit (saved by Fritzing 1.0.7)

parts:
  DISC1 = Mist Maker Piezo Disc [part_number="piezo mesh atomizer disc"]  # not connected
  MIST1 = Mist Maker Battery Kit V0.4.1 [part_number=byproductlab-mistmaker-battkit-v041]
  Part1 = Arduino Uno (Rev3)

nets:
  N1: MIST1.D0_/_MIST, Part1.D9_PWM
  N2: MIST1.D3_/_BOOST_EN, Part1.D7
  N3: MIST1.5V_in, Part1.5V
  GND: MIST1.GND, Part1.GND

custom parts:
  Mist Maker Piezo Disc: Ultrasonic mesh atomizer disc (108.7 kHz) with molded cable and PH-2.0 plug. Seat the plug into the Mist Maker kits' DISC connector.
  Mist Maker Battery Kit V0.4.1: Programmable Mist Maker Battery Kit (OSHWA US002742). Jumper into the empty XIAO socket: minimal mist = GND + D0 (108.7 kHz PWM) + D3 (boost enable HIGH). Use with the MistMaker Arduino library v2.5.0+.
